# Fritzing sketch schema (saved by Fritzing 1.0.4)
breadboards: 1

parts:
  Air_valve_(24_V_18_5_W) = Solenoid
  24_V = Power plug
  Atmospheric_valve_(24_V_18_5_W) = Solenoid
  Pressure_valve_(24_V_18_5_W) = Solenoid
  J4 = screw terminal, 4 pins
  J5 = screw terminal, 4 pins
  Lower_sensor = Pushbutton [package="[THT]"]
  Higher_sensor = Pushbutton [package="[THT]"]
  Part1 = Arduino Uno (Rev3) - ICSP
  8_Channel_Relay1 = 8 Channel Power Relay

nets:
  N1: Air_valve_(24_V_18_5_W).pin1, 8_Channel_Relay1.NO#23
  N2: Air_valve_(24_V_18_5_W).pin2, J4.pin2
  N3: 24_V.GND, J5.pin1
  N4: 24_V.VCC, J4.pin1
  N5: Atmospheric_valve_(24_V_18_5_W).pin1, 8_Channel_Relay1.NO#29
  N6: Atmospheric_valve_(24_V_18_5_W).pin2, J4.pin4
  N7: Pressure_valve_(24_V_18_5_W).pin1, 8_Channel_Relay1.NO#26
  N8: Pressure_valve_(24_V_18_5_W).pin2, J4.pin3
  N9: J5.pin2, 8_Channel_Relay1.COM#28
  N10: J5.pin3, 8_Channel_Relay1.COM#25
  N11: J5.pin4, 8_Channel_Relay1.COM#22
  GND: Lower_sensor.Pin_1, Lower_sensor.Pin_2, Higher_sensor.Pin_1, Higher_sensor.Pin_2, Part1.GND, 8_Channel_Relay1.GND
  N12: Lower_sensor.Pin_3, Lower_sensor.Pin_4, Part1.D6_PWM
  N13: Higher_sensor.Pin_3, Higher_sensor.Pin_4, Part1.D5_PWM
  N14: Part1.D2, 8_Channel_Relay1.IN3
  N15: Part1.D3_PWM, 8_Channel_Relay1.IN2
  N16: Part1.D4, 8_Channel_Relay1.IN1
  5V: Part1.5V, 8_Channel_Relay1.VCC

custom parts:
  8 Channel Power Relay: An 8 channel power relay. The module operates at 5V.
